# Fritzing sketch estacao_meteorologica_monster (saved by Fritzing 0.9.10b)
breadboards: 1

parts:
  Componente1 = Arduino Mega 2560 (Rev3)
  Componente2 = MQ-3 breakout
  Componente3 = MQ-4 breakout
  Componente4 = MQ-7 breakout
  Componente5 = MQ-9 breakout
  Componente7 = MQ-9 breakout
  Componente8 = MQ-9 breakout
  Componente9 = MQ-9 breakout
  M2 = BME280
  DHT1 = DHT22 Humidity and Temperature Sensor
  OLED_I2C1 = OLED 128x64 I2C Monochrome Display
  M3 = NEO-6M GPS Module [part_number=GY-GPS6MV2]
  Componente10 = HMC5883L Triple-axis Magnetometer [part_number=1746]
  Componente11 = BH1750
  Componente12 = FC-28 Soil Hygrometer Module - Probe
  A1 = GUVA-S12SD
  DS1 = DS18B20 1-Wire Temperature Sensor Probe
  R1 = Resistor [tolerance=±5% resistance=220k package="0402 [SMD]"]
  LED1 = RGB LED - (4 legs) [package="5 mm [THT]"]
  R2 = Resistor [tolerance=±5% resistance=220 package="0402 [SMD]"]
  R3 = Resistor [tolerance=±5% resistance=220 package="0402 [SMD]"]
  R4 = Resistor [tolerance=±5% resistance=220 package="0402 [SMD]"]
  Componente13 = MQ-7 breakout
  부품3 = FC-28 Soil Hygrometer Module

nets:
  N1: Componente1.A8, Componente9.AO
  N2: Componente1.A9, Componente5.AO
  N3: Componente1.A10, A1.Pin_1
  N4: Componente1.A11, 부품3.AO
  N5: Componente1.A0, Componente2.AO
  N6: Componente1.A1, Componente3.AO
  N7: Componente1.A2, Componente4.AO
  N8: Componente1.A3, Componente13.AO
  N9: Componente1.A4, M2.SDA
  N10: Componente1.A5, M2.SCL
  N11: Componente1.A6, Componente7.AO
  N12: Componente1.A7, Componente8.AO
  N13: Componente1.D21/SCL, Componente1.SCL, OLED_I2C1.SCK, Componente10.SCL, Componente11.SCL
  N14: Componente1.D20/SDA, Componente1.SDA, OLED_I2C1.SDA, Componente10.SDA, Componente11.SDA
  N15: Componente1.D17_PWM/RX2, M3.Tx
  N16: Componente1.D16_PWM/TX2, M3.Rx
  GND: Componente1.GND, Componente2.GND, Componente3.GND, Componente4.GND, Componente5.GND, Componente7.GND, Componente8.GND, Componente9.GND, M2.GND, DHT1.GND, OLED_I2C1.GND, M3.GND, Componente10.GND, Componente11.GND, A1.Pin_2, DS1.GND, LED1.common_anode, Componente13.GND, 부품3.GND
  3V3: Componente1.3V3, M2.VIN
  VCC: Componente1.5V, Componente2.VCC, Componente3.VCC, Componente4.VCC, Componente5.VCC, Componente7.VCC, Componente8.VCC, Componente9.VCC, DHT1.VDD, OLED_I2C1.VDD, M3.Vcc, Componente10.VIN, Componente11.VCC, A1.Pin_3, DS1.VDD, R1.Pin_0, Componente13.VCC, 부품3.VCC
  N17: Componente1.D22, DHT1.DATA
  N18: Componente1.D23, R2.Pin_0
  N19: Componente1.D25, R3.Pin_0
  N20: Componente1.D26, R4.Pin_0
  N21: Componente1.D28, DS1.DQ, R1.Pin_1
  N22: Componente12.POS, 부품3.POS
  N23: Componente12.NEG, 부품3.NEG
  N24: LED1.red_cathode, R2.Pin_1
  N25: LED1.green_cathode, R3.Pin_1
  N26: LED1.blue_cathode, R4.Pin_1

notes:
  MQ-135
  MQ-8
  MQ-131
  MQ-136
  Umidade do Solo
  Temperatura
  Umidade
  Temperatura Liquído
  Luminosidade
  UV
  Bússola
  Pressão
  Altitude
  LED RGB
  Display OLED
  GPS
  Latitude
  Longitude
  Velocidade
  Microcontrolador
  MQ-3
  Álcool
  Benzeno
  Hexano
  MQ-4
  Metano
  Fumaça
  MQ-135
  Dióxido de Carbono
  Tolueno
  Amônia
  MQ-7
  Monóxido de Carbono
  MQ-8
  Hidrogênio
  MQ-9
  GLP
  MQ-131
  Ozônio
  Cloro
  NOx
  MQ-136
  Sulfeto de Hidrogênio

custom parts:
  MQ-3 breakout: Alcohol sensor is capable of detecting alcohol (ethanol) particles on itself and gives the information in digital form back to us to manipulate with it. SKU:101251 • Voltage: 5V DC • Power: max 750mW • Measurement range: 0.04-4mg/L
  MQ-4 breakout: Created fron e-radionica MQ-7 breakout
  MQ-7 breakout: SKU: 101282
  MQ-9 breakout: SKU: 101284
  BME280: Temperature Humidity Barometric presure Sensor
  NEO-6M GPS Module: GY-GPS6MV2 NEO-6M GPS Module Module based on U-blox NEO-6M GPS engine, incorporating regulator for 3.3-5V DC input, MS621FE-compatible rechargeable battery for backup and EEPROM for storing configuration settings. Links: NEO-6 series product information page NEO-6 Datasheet
  HMC5883L Triple-axis Magnetometer: A magnetometer can sense where the strongest magnetic force is coming from, generally used to detect magnetic north. We based this breakout on a popular and well loved magnetometer, the HMC5883L. This compact sensor uses I2C to communicate and its very easy to use. Since it's a 3.3V max chip, we added circuitry to make it 5V-safe logic and power, for easy use with either 3 or 5V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
  BH1750: Light Sensor
  FC-28 Soil Hygrometer Module - Probe: The FC-28 is a soil hygrometer module that uses the Texas Instruments LM393 comparator chip to provide an analog measurement of soil humidity.
  GUVA-S12SD: GUVA-S12SD S12SD UV Detection Light Intensity Sensor Ultraviolet.
  FC-28 Soil Hygrometer Module: The FC-28 is a soil hygrometer module that uses the Texas Instruments LM393 comparator chip to provide an analog measurement of soil humidity. The digital output is high when soil moisture is over a certain threshold, as determined by adjusting the potentiometer.
